# Fritzing sketch Schéma de câblage (saved by Fritzing 0.9.3b)
breadboards: 1

parts:
  MKRFox1 = Arduino MKR Fox 1200
  IC1 = Voltage Regulator [package=78xxl]
  VCC1 = Battery
  Q1 = NPN-Transistor [package="TO92 [THT]"]
  R1 = Resistor [tolerance=±5% resistance=10 package="1206 [SMD]"]
  R2 = Resistor [tolerance=±5% resistance=100k package="1206 [SMD]"]
  R3 = Resistor [tolerance=±5% resistance=150 package=THT]
  J1 = shrouded pin header, 10 pins [form="♂ (shrouded male)"]

nets:
  N1: MKRFox1.DAC0/A0, R3.Pin_0, J1.pin2
  N2: MKRFox1.7, R1.Pin_1, R2.Pin_0
  GND: MKRFox1.GND, IC1.GND, VCC1.-, Q1.E, R2.Pin_1, R3.Pin_1
  N3: MKRFox1.VIN, IC1.OUT
  N4: IC1.IN, VCC1.+, J1.pin1
  N5: Q1.B, R1.Pin_0
  N6: Q1.C, J1.pin3
